// Logisim project Last.circ as structural Verilog: 1 circuit, main circuit main
module main (
);

  wire cdm_16_1_p2, cdm_16_1_p3, cdm_16_1_p5, cdm_16_1_p6, cdm_16_1_p7, cdm_16_1_p8, cdm_16_1_p9,
       cdm_16_1_p10, cdm_16_1_p11, cdm_16_1_p12, cdm_16_1_p14, cdm_16_1_p15, clock, mem, not_1_out, ozu_mem,
       program_mem, pzu_mem, read, uart_1_p3, word;
  wire [15:0] address_bus, cdm_16_1_p19, cdm_16_1_p20, data_bus;

  // Probe on cdm_16_1_p3
  // Probe on cdm_16_1_p2
  // Probe on cdm_16_1_p6
  // Probe on cdm_16_1_p5
  // CdM_16 cdm_16_1: pin names not known; wires that end beside it: 6'b000101, cdm_16_1_p2, cdm_16_1_p3, clock, cdm_16_1_p5, cdm_16_1_p6, cdm_16_1_p7, cdm_16_1_p8, cdm_16_1_p9, cdm_16_1_p10, cdm_16_1_p11, cdm_16_1_p12, cdm_16_1_p12, cdm_16_1_p14, cdm_16_1_p15, read, word, address_bus, cdm_16_1_p19, cdm_16_1_p20
  Clock clock_1 (.out(clock));
  // Probe on cdm_16_1_p8
  and and_1 (program_mem, address_bus[8], address_bus[9], address_bus[10], address_bus[11], address_bus[12], address_bus[13], address_bus[14], address_bus[15], mem);
  // Probe on cdm_16_1_p7
  // Probe on cdm_16_1_p9
  and and_2 (ozu_mem, mem, ~program_mem);  // AND_Gate
  // Probe on cdm_16_1_p10
  // Probe on cdm_16_1_p11
  assign cdm_16_1_p20 = read ? data_bus : 16'bz;  // Controlled_Buffer controlled_buffer_1
  Decoder #(.disabled(0)) decoder_1 (.out0(pzu_mem), .out1(mem), .sel(cdm_16_1_p14), .en(cdm_16_1_p15));
  assign data_bus = not_1_out ? cdm_16_1_p19 : 16'bz;  // Controlled_Buffer controlled_buffer_2
  not not_1 (not_1_out, read);
  // Debugger debugger_1: pin names not known
  // UART uart_1: pin names not known; wires that end beside it: pzu_mem, clock, uart_1_p3
  // RAM ram_1: pin names not known; wires that end beside it: address_bus, word, ozu_mem, clock, read, data_bus
  // ROM rom_1: pin names not known; wires that end beside it: address_bus, word, data_bus
  LED led_1 (.in(uart_1_p3));

  // Other names for the same wires on the sheet: address_bus_prog[7:0] = address_bus[7:0]
endmodule
